// Logisim project count.circ as structural Verilog: 3 circuits, main circuit Count
module Test_Count (
);

  wire Clk_out, count_1_rdy, tester_1_clk_out, tester_1_fail, tester_1_start, tester_1_success;
  wire [3:0] count_1_c;
  wire [31:0] tester_1_x;

  // Probe on tester_1_x
  Clock Clk (.out(Clk_out));
  LED led_1 (.in(tester_1_fail));
  Count count_1 (.x(tester_1_x), .clk(tester_1_clk_out), .start(tester_1_start), .c(count_1_c), .rdy(count_1_rdy));
  tester tester_1 (
    .clk_in(Clk_out), .z(count_1_c), .rdy(count_1_rdy), .x(tester_1_x), .start(tester_1_start),
    .clk_out(tester_1_clk_out), .fail(tester_1_fail), .success(tester_1_success));
  LED led_2 (.in(tester_1_success));
  // Probe on count_1_c
  // Probe on count_1_c
  // Probe on count_1_rdy

  // Notes on the sheet:
  //   Red means failure:
  //   the outputs z or rdy
  //   wrong for the input x.
  //   You need to debug your circuit.
  //   the full timing diagram
  //   Congratulations!
  //   Green means success
  //   Your solution matches
  //   To debug your circuit
  //   enter to the module Count
  //   with the hand from here,
  //   not from the left panel.
endmodule

module Count (
  input  [31:0] x,
  input  clk,
  input  start,
  output rdy,
  output [3:0] c
);

  wire and_1_out, comparator_2_eq, or_1_out;
  wire [3:0] adder_1_out, bit_extender_1_out, multiplexer_3_out;
  wire [15:0] multiplexer_2_out, set_q, shifter_2_out, x16_2_out, x16_3_out, x16_out;
  wire [31:0] multiplexer_1_out, rx_q, shifter_1_out;

  // Probe on x
  Shifter #(.width(32), .shift("lr")) shifter_1 (.in(rx_q), .\dist (5'b00100), .out(shifter_1_out));
  assign x16_out = shifter_2_out | set_q;  // OR_Gate x16, 16 bits wide
  Multiplexer #(.width(32), .enable("false")) multiplexer_1 (
    .in0(shifter_1_out), .in1(x), .out(multiplexer_1_out), .sel(start));
  Multiplexer #(.width(16), .disabled(0), .enable("false")) multiplexer_2 (
    .in0(x16_out), .in1({16{1'b0}}), .out(multiplexer_2_out), .sel(start));
  Multiplexer #(.width(4), .disabled(0), .enable("false")) multiplexer_3 (
    .in0(adder_1_out), .in1(4'b0000), .out(multiplexer_3_out), .sel(start));
  Register #(.width(32), .trigger("falling")) rx (.D(multiplexer_1_out), .Q(rx_q), .clk(clk));  // open: en, clr
  Bit_Extender #(.in_width(32), .out_width(4)) bit_extender_1 (.in(rx_q), .out(bit_extender_1_out));
  Register #(.width(16), .trigger("falling")) set (
    .D(multiplexer_2_out), .en(or_1_out), .Q(set_q), .clk(clk));  // open: clr
  Register #(.width(4), .trigger("falling")) u_c (.D(multiplexer_3_out), .en(or_1_out), .Q(c), .clk(clk));  // open: clr
  Comparator #(.width(32)) comparator_1 (.a({32{1'b0}}), .b(rx_q), .eq(rdy));  // open: gt, lt
  Shifter #(.width(16)) shifter_2 (.in(16'h1), .\dist (bit_extender_1_out), .out(shifter_2_out));
  Adder #(.width(4)) adder_1 (.a(4'b0001), .b(c), .out(adder_1_out));  // open: cin, cout
  assign x16_2_out = set_q | 16'h1;  // OR_Gate x16_2, 16 bits wide
  or or_1 (or_1_out, and_1_out, start);
  assign x16_3_out = shifter_2_out & x16_2_out;  // AND_Gate x16_3, 16 bits wide
  and and_1 (and_1_out, ~rdy, comparator_2_eq);  // AND_Gate
  Comparator #(.width(16)) comparator_2 (.a({16{1'b0}}), .b(x16_3_out), .eq(comparator_2_eq));  // open: gt, lt

  // Notes on the sheet:
  //   Complete el circuito
  //   c = c+1;
  //   }
  //   Calcule rdy de 1 bit = (x == 0)
  //   if ( start || (!rdy && new) )  {
  //   set = set | mask;
  //   rx = start ? x : (rx >> 4);
  //   mask de 16 bits está calculado como 1 << (rx & 0xf)
  //   Calcule new de 1 bit = ((set|1) & mask) == 0
  //   h=rx & 0xf
  //   start || (!rdy && new)
  //   Calcule los registros set, c y rx en el pulso de bajada del reloj como:
  //   fin del while
  //   mask = 1<<h
  //   mask
  //   eso define el final del cálculo
  //   // Esta condición está conectada a la entrada 'en' de set y c
  //   se cumple el if
  //   !rdy && new
  //   start
  //   !rdy
  //   new
  //   To debug your circuit
  //   Programa en C:
  //   int count(uint x) {
  //   uint rx= x;
  //   ushort set= 0;
  //   int c= 0;
  //   while (rx!=0) {
  //   }
  //   rx >>= 4;
  //   }
  //   return c;
  //   }
  //   and then enter to the module Count
  //   with the hand, not from the left panel.
  //   Advance the clock with control-T
  //   Restart the simulation with control-R
  //   uint h= rx & 0xf;
  //   mask= 1<<h;
  //   set |= mask;
  //   c++;
  //   Con estas compuertas se puede resolver
  //   el problema, pero puedes usar otras.
  //   select the module test-group from the left panel
  //   if ((set | 1) & mask) == 0) { // set|1 es para no contar las cifras 0
endmodule

module tester (
  input  rdy,
  input  [3:0] z,
  input  clk_in,
  output [31:0] x,
  output start,
  output success,
  output fail,
  output clk_out
);

  wire and_1_out, comparator_1_eq, d_ff_1_q;
  wire [4:0] counter_1_q;
  wire [23:0] rom_1_data;

  Pull_Resistor #(.pull(1)) pull_resistor_1 (.node(rdy));
  Pull_Resistor pull_resistor_2 (.node(z));
  D_Flip_Flop #(.trigger("falling")) d_ff_1 (.clk(clk_in), .D(1'b1), .Q(d_ff_1_q));  // open: Qn, preset, en, reset
  and and_1 (and_1_out, d_ff_1_q, rdy, ~fail, ~rom_1_data[12]);  // AND_Gate
  Counter #(.width(5), .max('h1f), .trigger("falling")) counter_1 (
    .count(and_1_out), .Q(counter_1_q), .clk(clk_in));  // open: load, D, carry, clr
  ROM #(.addrWidth(5), .dataWidth(24)) rom_1 (
    .addr(counter_1_q), .data({rom_1_data[23:9], start, rom_1_data[7:0]}));  // open: sel
  Comparator #(.width(4)) comparator_1 (.a(rom_1_data[19:16]), .b(z), .eq(comparator_1_eq));  // open: gt, lt
  ROM #(.addrWidth(3), .dataWidth(32)) rom_2 (.addr(rom_1_data[2:0]), .data(x));  // open: sel
  and and_2 (success, rom_1_data[12], rdy, comparator_1_eq);
  and and_3 (fail, rom_1_data[4], rdy, ~comparator_1_eq);  // AND_Gate
  and and_4 (clk_out, ~fail, clk_in);  // AND_Gate

  // Notes on the sheet:
  //   c[19:16] success[12] start[8] valid[4] ex[2:0] 
  //   contents of rom_1 (hex, n*v repeats v):
  //   0 100 10 10 101 10011 102 10012 10012 103 20013 20013 104 30014 105 80015 80015 80015 81015
  //   contents of rom_2 (hex, n*v repeats v):
  //   0 b bb 7bb 310f11f 12345678
endmodule
